# Fritzing sketch Camera_Fritzing_Schematic (saved by Fritzing 0.7.10b)
breadboards: 1

parts:
  U1 = atmega328 [package=dip]
  ISP1 = shrouded pin header, 6 pins [form="♂ (shrouded male)"]  # not connected
  VCC1 = Battery
  J1 = Basic Servo

nets:
  GND: U1.RESET, U1.GND, VCC1.-, J1.gnd
  VCC: U1.VCC, U1.AVCC, U1.AREF, VCC1.+, J1.vcc
